// Logisim project s-mips - con Cache - Copy.circ as structural Verilog: 16 circuits, main circuit S-MIPS Board
module S_MIPS_Board (
  output halt
);

  wire button_1_out, CLK, CS, d_ff_1_q, R_W, Reset_out, RST, TTY_EN;
  wire [2:0] KDB;
  wire [3:0] Mask, ram_1_read_time, ram_1_write_time;
  wire [6:0] KDB_DATA, TTY_DATA;
  wire [15:0] Addr;
  wire [31:0] ram_1_data_out_0, ram_1_data_out_1, ram_1_data_out_2, ram_1_data_out_3, s_mips_1_ram_in_0,
       s_mips_1_ram_in_1, s_mips_1_ram_in_2, s_mips_1_ram_in_3;

  TTY #(.rows(25), .cols(80)) tty_1 (.data(TTY_DATA), .clk(CLK), .we(TTY_EN), .clr(RST));
  RAM ram_1 (
    .Address(Addr), .Data_Out_0(ram_1_data_out_0), .Data_Out_1(ram_1_data_out_1),
    .Data_Out_2(ram_1_data_out_2), .Data_Out_3(ram_1_data_out_3), .Data_In_0(s_mips_1_ram_in_0),
    .Data_In_1(s_mips_1_ram_in_1), .Data_In_2(s_mips_1_ram_in_2), .Data_In_3(s_mips_1_ram_in_3), .Mask(Mask),
    .nRead_Write(R_W), .Chip_Select(CS), .Read_Time(ram_1_read_time), .Reset(button_1_out),
    .Write_Time(ram_1_write_time));
  Button button_1 (.out(button_1_out));
  Keyboard #(.buflen(64)) keyboard_1 (.clk(CLK), .re(KDB[0]), .avail(KDB[2]), .data(KDB_DATA));  // open: clr
  S_MIPS s_mips_1 (
    .Kbd_Enable(KDB[0]), .Address(Addr), .Kbd_Clear(KDB[1]), .Kbd_Available(KDB[2]),
    .RAM_In_0(s_mips_1_ram_in_0), .Kbd_ASCII_Data(KDB_DATA), .RAM_In_1(s_mips_1_ram_in_1),
    .TTY_Enable(TTY_EN), .RAM_In_2(s_mips_1_ram_in_2), .RAM_In_3(s_mips_1_ram_in_3),
    .TTY_ASCII_Data(TTY_DATA), .Reset(RST), .RAM_Out_0(ram_1_data_out_0), .Clock(CLK),
    .RAM_Out_1(ram_1_data_out_1), .Stop(halt), .RAM_Out_2(ram_1_data_out_2), .RAM_Out_3(ram_1_data_out_3),
    .Mask(Mask), .Read_Time(ram_1_read_time), .Write_Time(ram_1_write_time), .nRead_Write(R_W),
    .Chip_Select(CS));
  D_Flip_Flop d_ff_1 (.clk(CLK), .D(1'b1), .Q(d_ff_1_q), .reset(Reset_out));  // open: Qn, preset, en
  Button Reset (.out(Reset_out));
  Clock clock_1 (.out(CLK));
  D_Flip_Flop d_ff_2 (.clk(CLK), .D(d_ff_1_q), .Qn(RST), .reset(Reset_out));  // open: Q, preset, en

  // Notes on the sheet:
  //   NO MODIFICAR
  //   Keyboard
endmodule

module RAM (
  input  [15:0] Address,
  input  [31:0] Data_In_0,
  input  [31:0] Data_In_1,
  input  [31:0] Data_In_2,
  input  [31:0] Data_In_3,
  input  [3:0] Mask,
  input  nRead_Write,
  input  Chip_Select,
  input  Reset,
  output [31:0] Data_Out_0,
  output [31:0] Data_Out_1,
  output [31:0] Data_Out_2,
  output [31:0] Data_Out_3,
  output [3:0] Read_Time,
  output [3:0] Write_Time
);

  wire and_2_out, and_3_out, and_4_out, and_5_out, and_6_out, and_7_out, and_8_out, and_9_out, Changed, CLK,
       comparator_2_eq, comparator_3_eq, comparator_4_eq, comparator_5_eq, comparator_6_eq, Count,
       demultiplexer_3_out0, Idle, Idle_q, Load, Load0, Load1, nand_1_out, or_1_out, or_2_out, or_3_out,
       or_4_out, or_5_out, or_6_out, or_7_out, or_8_out, or_9_out, or_10_out, Proc_q, Update_Mem, Zero_Time;
  wire [3:0] counter_1_q, multiplexer_1_out, subtractor_1_out;
  wire [31:0] register_1_q, register_2_q, register_3_q, register_4_q, register_5_q;

  // Probe on 4'b0011
  // Probe on 4'b0101
  Multiplexer #(.width(4), .enable("false")) multiplexer_1 (
    .in0(4'b0011), .in1(4'b0101), .out(multiplexer_1_out), .sel(nRead_Write));
  or or_1 (or_1_out, Idle, Update_Mem);
  or or_2 (or_2_out, ~Chip_Select, Reset);  // OR_Gate
  Subtractor #(.width(4)) subtractor_1 (.a(multiplexer_1_out), .b(4'b0010), .out(subtractor_1_out));  // open: bin, bout
  Demultiplexer #(.enable("false")) demultiplexer_1 (.out0(Idle), .out1(Load0), .in(Idle_q), .sel(Changed));
  D_Flip_Flop u_Idle (.clk(CLK), .D(or_1_out), .Q(Idle_q), .preset(or_2_out));  // open: Qn, en, reset
  // Probe on counter_1_q
  Counter #(.width(4), .max('hf)) counter_1 (
    .load(Load), .D(subtractor_1_out), .count(Count), .Q(counter_1_q), .clk(CLK), .clr(or_3_out));  // open: carry
  or or_3 (or_3_out, ~Chip_Select, Reset);  // OR_Gate
  Comparator #(.width(4), .mode("unsigned")) comparator_1 (
    .a(4'b0000), .b(counter_1_q), .eq(Zero_Time));  // open: gt, lt
  or or_4 (or_4_out, Count, Load0, Load1);
  Register #(.width(32)) register_1 (.D(Data_In_0), .en(Chip_Select), .Q(register_1_q), .clk(CLK), .clr(or_5_out));
  or or_5 (or_5_out, ~Chip_Select, Reset);  // OR_Gate
  Register #(.width(32)) register_2 (.D(Data_In_1), .en(Chip_Select), .Q(register_2_q), .clk(CLK), .clr(or_6_out));
  or or_6 (or_6_out, ~Chip_Select, Reset);  // OR_Gate
  Register #(.width(32)) register_3 (.D(Data_In_2), .en(Chip_Select), .Q(register_3_q), .clk(CLK), .clr(or_7_out));
  or or_7 (or_7_out, ~Chip_Select, Reset);  // OR_Gate
  Register #(.width(32)) register_4 (.D(Data_In_3), .en(Chip_Select), .Q(register_4_q), .clk(CLK), .clr(or_8_out));
  or or_8 (or_8_out, ~Chip_Select, Reset);  // OR_Gate
  Register #(.width(32)) register_5 (
    .D({{11{1'b1}}, nRead_Write, Mask, Address}), .en(Chip_Select), .Q(register_5_q), .clk(CLK),
    .clr(or_9_out));
  or or_9 (or_9_out, ~Chip_Select, Reset);  // OR_Gate
  D_Flip_Flop Proc (.clk(CLK), .D(or_4_out), .Q(Proc_q), .reset(or_10_out));  // open: Qn, preset, en
  or or_10 (or_10_out, ~Chip_Select, Reset);  // OR_Gate
  Demultiplexer #(.enable("false")) demultiplexer_2 (
    .out0(Count), .out1(Update_Mem), .in(demultiplexer_3_out0), .sel(Zero_Time));
  Demultiplexer #(.enable("false")) demultiplexer_3 (
    .out0(demultiplexer_3_out0), .out1(Load1), .in(Proc_q), .sel(Changed));
  Clock clock_1 (.out(CLK));
  Comparator #(.width(32)) comparator_2 (.a(register_1_q), .b(Data_In_0), .eq(comparator_2_eq));  // open: gt, lt
  Comparator #(.width(32)) comparator_3 (.a(register_2_q), .b(Data_In_1), .eq(comparator_3_eq));  // open: gt, lt
  Comparator #(.width(32)) comparator_4 (.a(register_3_q), .b(Data_In_2), .eq(comparator_4_eq));  // open: gt, lt
  Comparator #(.width(32)) comparator_5 (.a(register_4_q), .b(Data_In_3), .eq(comparator_5_eq));  // open: gt, lt
  Comparator #(.width(32)) comparator_6 (
    .a(register_5_q), .b({{11{1'b1}}, nRead_Write, Mask, Address}), .eq(comparator_6_eq));  // open: gt, lt
  nand nand_1 (nand_1_out, comparator_6_eq, comparator_2_eq, comparator_3_eq, comparator_4_eq, comparator_5_eq);
  and and_1 (Changed, nand_1_out, Chip_Select);
  or or_11 (Load, Count, Load1, Load0);
  and and_2 (and_2_out, Mask[0], Update_Mem, nRead_Write);
  and and_3 (and_3_out, Mask[1], Update_Mem, nRead_Write);
  and and_4 (and_4_out, Mask[2], Update_Mem, nRead_Write);
  and and_5 (and_5_out, Mask[3], Update_Mem, nRead_Write);
  RAM_part #(.addrWidth(16), .dataWidth(32), .bus("separate")) ram_1 (
    .addr(Address), .din(Data_In_0), .data(Data_Out_0), .str(and_2_out), .sel(Chip_Select), .clk(CLK),
    .ld(and_6_out), .clr(Reset));
  and and_6 (and_6_out, ~nRead_Write, Idle);  // AND_Gate
  RAM_part #(.addrWidth(16), .dataWidth(32), .bus("separate")) ram_2 (
    .addr(Address), .din(Data_In_1), .data(Data_Out_1), .str(and_3_out), .sel(Chip_Select), .clk(CLK),
    .ld(and_7_out), .clr(Reset));
  and and_7 (and_7_out, ~nRead_Write, Idle);  // AND_Gate
  RAM_part #(.addrWidth(16), .dataWidth(32), .bus("separate")) ram_3 (
    .addr(Address), .din(Data_In_2), .data(Data_Out_2), .str(and_4_out), .sel(Chip_Select), .clk(CLK),
    .ld(and_8_out), .clr(Reset));
  and and_8 (and_8_out, ~nRead_Write, Idle);  // AND_Gate
  RAM_part #(.addrWidth(16), .dataWidth(32), .bus("separate")) ram_4 (
    .addr(Address), .din(Data_In_3), .data(Data_Out_3), .str(and_5_out), .sel(Chip_Select), .clk(CLK),
    .ld(and_9_out), .clr(Reset));
  and and_9 (and_9_out, ~nRead_Write, Idle);  // AND_Gate

  assign Read_Time = 4'b0011;
  assign Write_Time = 4'b0101;

  // Other names for the same wires on the sheet: M0 = Mask[0]; M1 = Mask[1]; M2 = Mask[2]; M3 = Mask[3];
  //   RW = nRead_Write; CLR = Reset; CS = Chip_Select; Load2 = Count

  // Notes on the sheet:
  //   NO MODIFICAR
  //   excepto quizás los valores RT y WT
  //   BANK0
  //   BANK1
  //   BANK2
  //   BANK3
endmodule

module S_MIPS (
  input  Kbd_Available,
  input  [6:0] Kbd_ASCII_Data,
  input  [31:0] RAM_Out_0,
  input  [31:0] RAM_Out_1,
  input  Reset,
  input  [31:0] RAM_Out_2,
  input  Clock,
  input  [31:0] RAM_Out_3,
  input  [3:0] Read_Time,
  input  [3:0] Write_Time,
  output Kbd_Enable,
  output [15:0] Address,
  output Kbd_Clear,
  output TTY_Enable,
  output [6:0] TTY_ASCII_Data,
  output Stop,
  output [31:0] RAM_In_0,
  output [31:0] RAM_In_1,
  output [31:0] RAM_In_2,
  output [31:0] RAM_In_3,
  output [3:0] Mask,
  output nRead_Write,
  output Chip_Select
);

  wire add, addi, \and , and_4_out, and_5_out, andi, beq, bgtz, blez, bltz, bne, CLK, CS0, CS2, cu_beq,
       cu_bgtz, cu_blez, cu_bltz, cu_bne, cu_jmp, cu_jr, div, divu, EnIF, EnInst, EnRM, EnRnd, EnSp, EnWM,
       eq, gtz, halt, InstR, jmp, jr, kbd, lez, ltz, lw, MemR, MemR1, MemR2, mfhi, mflo, minus_1, mult, mulu,
       ne, Next, nop, \nor , NxtIns, \or , or_3_out, or_5_out, or_6_out, or_7_out, or_8_out, or_9_out,
       or_13_out, or_14_out, ori, pop, popRF, push, pushRf, R_W, Ready_Cache, rnd, sgn, slt, slti, sltiu,
       sltu, sub, sw, tty, \xor , xori;
  wire [2:0] or_10_out;
  wire [3:0] OpCode;
  wire [4:0] multiplexer_2_out, RdDir, RsDir, RtDir, XDir;
  wire [15:0] InstAd, multiplexer_3_out, ReadMemAd, WriteMemAd;
  wire [25:0] DstJp;
  wire [31:0] adder_1_out, bit_extender_1_out, ca2, Cache_OUTPUT_0, Cache_OUTPUT_1, Cache_OUTPUT_2,
       Cache_OUTPUT_3, Data, dir, Hi, instruction_fetcher_1_instruction, Lo, multiplexer_1_out,
       multiplexer_4_out, multiplexer_6_out, PC_Out, PCIn, RAM_Out, random_1_out, Result, RHi, RLo, RSP, RT;
  wire [31:7] RS;

  or or_1 (Chip_Select, CS0, nRead_Write, CS2);
  Multiplexer #(.width(32)) multiplexer_1 (
    .in0(RT), .in1({RS, TTY_ASCII_Data}), .out(multiplexer_1_out), .sel(push));  // open: en
  and and_1 (CLK, Clock, ~Stop);  // AND_Gate
  Program_Counter program_counter_1 (.PC_In(PCIn), .Enable(NxtIns), .Clock(CLK), .Clear(Reset), .PC_Out(PC_Out));
  // Probe on PC_Out
  Branch_Control branch_control_1 (
    .Beq(cu_beq), .Eq(eq), .Bne(cu_bne), .Ne(ne), .Blez(cu_blez), .Next_Inst(NxtIns), .Lez(lez),
    .Bgtz(cu_bgtz), .Gtz(gtz), .Bltz(cu_bltz), .Jump(cu_jmp), .Jmp_Re(cu_jr), .Ltz(ltz), .Offset(ca2),
    .PC_In(PC_Out), .RS({RS, TTY_ASCII_Data}), .Destino_Salto(DstJp), .PC_Out(PCIn));
  Write_Memory write_memory_1 (
    .Data(multiplexer_1_out), .Direction(dir), .Clock(CLK), .Enable(EnWM), .Reset(Reset),
    .Write_Time(Write_Time), .Mask(Mask), .Ram_1(RAM_In_0), .Address(WriteMemAd), .Ram_2(RAM_In_1),
    .Ram_3(RAM_In_2), .Finish(MemR1), .Ram_4(RAM_In_3), .CS(nRead_Write));
  Instruction_Cache instruction_cache_1 (
    .Clock(CLK), .Ram_0(RAM_Out_0), .Enable(EnIF), .Reset(Reset), .Read_Time(Read_Time), .Ram_1(RAM_Out_1),
    .Ram_2(RAM_Out_2), .Ram_3(RAM_Out_3), .PC(PC_Out), .Cache_Out_0(Cache_OUTPUT_0),
    .Cache_Out_1(Cache_OUTPUT_1), .Cache_Out_2(Cache_OUTPUT_2), .Cache_Out_3(Cache_OUTPUT_3),
    .Address(InstAd), .Chip_Select(CS0), .Finish(Ready_Cache), .Dirty(nRead_Write));
  or or_2 (NxtIns, MemR2, Next, MemR1);
  Instruction_Fetcher instruction_fetcher_1 (
    .Ram_1(Cache_OUTPUT_0), .Clock(CLK), .Enable(Ready_Cache), .Ram_2(Cache_OUTPUT_1), .Reset(Reset),
    .Ram_3(Cache_OUTPUT_2), .Ram_4(Cache_OUTPUT_3), .PC(PC_Out),
    .Instruction(instruction_fetcher_1_instruction), .Finish(InstR));
  // Probe on instruction_fetcher_1_instruction
  Read_Memory read_memory_1 (
    .Ram_1(RAM_Out_0), .Clock(CLK), .Enable(EnRM), .Ram_2(RAM_Out_1), .Reset(Reset), .Read_Time(Read_Time),
    .Ram_3(RAM_Out_2), .Ram_4(RAM_Out_3), .Address_In(dir), .Finish(MemR2), .Chip_Select(CS2),
    .Ram_Out(RAM_Out), .Address_Out(ReadMemAd));
  Control_Unit control_unit_1 (
    .nop(nop), .halt(halt), .add(add), .kbd(kbd), .sub(sub), .rnd(rnd), .mul(mult), .tty(tty), .mulu(mulu),
    .j(jmp), .div(div), .addi(addi), .divu(divu), .andi(andi), .\and (\and ), .ori(ori), .\or (\or ),
    .xori(xori), .\nor (\nor ), .slti(slti), .\xor (\xor ), .sltiu(sltiu), .push(push), .lw(lw), .pop(pop),
    .sw(sw), .slt(slt), .beq(beq), .sltu(sltu), .bne(bne), .jr(jr), .blez(blez), .mfhi(mfhi), .bgtz(bgtz),
    .mflo(mflo), .bltz(bltz), .Instr_Ready(InstR), .Mem_Ready(MemR), .Clock(CLK), .jump(cu_jmp),
    .jump_register(cu_jr), .EnKbd(Kbd_Enable), .beq_2(cu_beq), .Stop(Stop), .EnRnd(EnRnd), .bne_2(cu_bne),
    .blez_2(cu_blez), .bgtz_2(cu_bgtz), .EnTTY(TTY_Enable), .bltz_2(cu_bltz), .EnRM(EnRM), .EnWM(EnWM),
    .Pop_2(popRF), .Push_2(pushRf), .Sign(sgn), .EnableSP(EnSp), .OpCode(OpCode), .EnInstruction(EnInst),
    .Next(Next), .R_W(R_W));
  Instruction_Decoder instruction_decoder_1 (
    .in_1(instruction_fetcher_1_instruction), .nop(nop), .add(add), .sub(sub), .mult(mult), .div(div),
    .mulu(mulu), .divu(divu), .slt(slt), .sltu(sltu), .\and (\and ), .\or (\or ), .\nor (\nor ),
    .\xor (\xor ), .addi(addi), .sltiu(sltiu), .slti(slti), .andi(andi), .ori(ori), .xori(xori), .lw(lw),
    .pop(pop), .push(push), .sw(sw), .bq(beq), .bne(bne), .blez(blez), .bltz(bltz), .bgtz(bgtz), .jr(jr),
    .mhfi(mfhi), .mflo(mflo), .halt(halt), .rnd(rnd), .tty(tty), .kbd(kbd), .Rd(RdDir), .Rt(RtDir),
    .Rs(RsDir), .X(XDir), .Destino_Salto(DstJp), .Constante_A2(ca2), .jump(jmp));
  and and_2 (minus_1, ~Kbd_Available, kbd);  // AND_Gate
  or or_3 (or_3_out, add, sub, mult, mulu, div, divu, slt, sltu, \and , \or , \nor , pop, rnd, kbd, mfhi, mflo, \xor );
  Multiplexer #(.width(5)) multiplexer_2 (
    .in0(RtDir), .in1(RdDir), .out(multiplexer_2_out), .sel(or_3_out));  // open: en
  Multiplexer #(.width(16)) multiplexer_3 (
    .in0(WriteMemAd), .in1(ReadMemAd), .out(multiplexer_3_out), .sel(EnRM));  // open: en
  or or_4 (MemR, MemR1, MemR2);
  assign bit_extender_1_out = {{25{1'b0}}, Kbd_ASCII_Data};  // Bit_Extender bit_extender_1
  Multiplexer #(.width(32)) multiplexer_4 (.in0(RT), .in1(ca2), .out(multiplexer_4_out), .sel(or_5_out));  // open: en
  or or_5 (or_5_out, xori, ori, andi, sltiu, slti, addi);
  Multiplexer #(.width(16)) multiplexer_5 (
    .in0(multiplexer_3_out), .in1(InstAd), .out(Address), .sel(CS0));  // open: en
  and and_3 (EnIF, ~or_7_out, or_8_out);  // AND_Gate
  Random #(.width(32)) random_1 (.clk(CLK), .next(EnRnd), .out(random_1_out));  // open: clr
  or or_6 (or_6_out, blez, bltz, bgtz);
  or or_7 (or_7_out, and_4_out, and_5_out);
  or or_8 (or_8_out, Reset, EnInst);
  or or_9 (or_9_out, lw, pop);
  Register_File register_file_1 (
    .Enable_H_L(OpCode[3]), .High(Hi), .R_W(R_W), .Register_02(RT), .Low(Lo), .Register_SP(RSP),
    .DA(multiplexer_2_out), .Register_Selector_01(RsDir), .Register_Selector_02(RtDir), .Clock(CLK),
    .Reset(Reset), .Pop(popRF), .Push(pushRf), .EnSP(EnSp), .Data(Data), .High_2(RHi),
    .Register_01({RS, TTY_ASCII_Data}), .Low_2(RLo));
  Multiplexer #(.width(32)) multiplexer_6 (
    .in0(multiplexer_4_out), .in1({32{1'b0}}), .out(multiplexer_6_out), .sel(or_6_out));  // open: en
  and and_4 (and_4_out, ~MemR2, EnRM);  // AND_Gate
  and and_5 (and_5_out, ~MemR1, or_14_out);  // AND_Gate
  Multiplexer #(.select(3), .width(32)) multiplexer_7 (
    .in0(Result), .in1(random_1_out), .in2(RHi), .in3(RLo), .in4(RAM_Out), .in5(bit_extender_1_out),
    .in7({32{1'b1}}), .out(Data), .sel(or_10_out));  // open: in6, en
  or or_10 (or_10_out[0], rnd, mflo, kbd);
  or or_11 (or_10_out[2], kbd, minus_1, or_9_out);
  or or_12 (or_10_out[1], mfhi, minus_1, mflo);
  // Probe on {RS, TTY_ASCII_Data}
  // Probe on RSP
  // Probe on Result
  ALU alu_1 (
    .X({RS, TTY_ASCII_Data}), .Y(multiplexer_6_out), .OP_Code(OpCode), .Result(Result), .High(Hi), .Low(Lo),
    .Eq(eq), .Ne(ne), .Lez(lez), .Ltz(ltz), .Sign(sgn), .Gtz(gtz));  // open: SF, ZF
  or or_13 (or_13_out, pop, push);
  Adder #(.width(32)) adder_1 (.a({RS, TTY_ASCII_Data}), .b(ca2), .out(adder_1_out));  // open: cin, cout
  or or_14 (or_14_out, EnWM, pushRf);
  // Probe on RT
  Multiplexer #(.width(32)) multiplexer_8 (.in0(adder_1_out), .in1(RSP), .out(dir), .sel(or_13_out));  // open: en

  assign Kbd_Clear = Reset;

  // Other names for the same wires on the sheet: CS = Chip_Select; KBD_AVAIL = Kbd_Available; CLR = Reset;
  //   KBD_CLR = Reset; KBD_DATA[6:0] = Kbd_ASCII_Data; RAM_A[15:0] = Address; RAM_INPUT_0[31:0] = RAM_In_0;
  //   RAM_INPUT_1[31:0] = RAM_In_1; RAM_INPUT_2[31:0] = RAM_In_2; RAM_INPUT_3[31:0] = RAM_In_3; RAM_MASK[3:0] = Mask;
  //   RAM_OUTPUT_0[31:0] = RAM_Out_0; RAM_OUTPUT_1[31:0] = RAM_Out_1; RAM_OUTPUT_2[31:0] = RAM_Out_2;
  //   RAM_OUTPUT_3[31:0] = RAM_Out_3; RS[6:0] = TTY_ASCII_Data; TTY_DATA[6:0] = TTY_ASCII_Data; CS1 = nRead_Write;
  //   RW = nRead_Write

  // Notes on the sheet:
  //   RAM ADDRESS
  //   DATA FROM RAM
  //   DATA TO RAM
  //   DATA WRITE MASK
  //   RAM TIMING
  //   RAM CONTROL
  //   KEYBOARD
  //   TTY
  //   SEQUENCING
endmodule

// R/W
module Control_Unit (
  input  nop,
  input  halt,
  input  add,
  input  kbd,
  input  sub,
  input  rnd,
  input  mul,
  input  tty,
  input  mulu,
  input  j,
  input  div,
  input  addi,
  input  divu,
  input  andi,
  input  \and ,
  input  ori,
  input  \or ,
  input  xori,
  input  \nor ,
  input  slti,
  input  \xor ,
  input  sltiu,
  input  push,
  input  lw,
  input  pop,
  input  sw,
  input  slt,
  input  beq,
  input  sltu,
  input  bne,
  input  jr,
  input  blez,
  input  mfhi,
  input  bgtz,
  input  mflo,
  input  bltz,
  input  Instr_Ready,
  input  Mem_Ready,
  input  Clock,
  output jump,
  output jump_register,
  output EnKbd,
  output beq_2,
  output Stop,
  output EnRnd,
  output bne_2,
  output blez_2,
  output bgtz_2,
  output EnTTY,
  output bltz_2,
  output EnRM,
  output EnWM,
  output Pop_2,
  output Push_2,
  output Sign,
  output EnableSP,
  output [3:0] OpCode,
  output EnInstruction,
  output Next,
  output R_W
);

  wire add_code1, add_code2, and_34_out, and_code1, and_code2, div_code2, EnRM1, EnRM2, EnWM1, EnWM2,
       mul_code, mulu_code, Next2, Next8, Next9, Next10, Next13, Next14, Next15, Next16, Next17, Next21,
       Next24, Next25, Next26, Next27, Next30, Next31, Next32, Next33, Next34, Next36, NxtIns, or_1_out,
       or_2_out, or_3_out, or_4_out, or_5_out, or_6_out, or_7_out, or_8_out;
  wire [3:0] priority_encoder_1_out;

  or or_1 (or_1_out, add_code1, add_code2);
  or or_2 (or_2_out, Next13, Next26);
  or or_3 (or_3_out, Next14, Next27);
  or or_4 (or_4_out, and_code1, and_code2);
  or or_5 (or_5_out, Next8, Next24);
  or or_6 (or_6_out, Next10, Next25);
  or or_7 (or_7_out, Sign, div_code2);
  and and_1 (add_code1, NxtIns, add);
  and and_2 (Next2, NxtIns, sub);
  and and_3 (mul_code, NxtIns, mul);
  and and_4 (mulu_code, NxtIns, mulu);
  and and_5 (Sign, NxtIns, div);
  and and_6 (div_code2, NxtIns, divu);
  and and_7 (and_code1, NxtIns, \and );
  and and_8 (Next8, NxtIns, \or );
  Priority_Encoder #(.select(4)) priority_encoder_1 (
    .in0(or_1_out), .in1(Next2), .in2(or_2_out), .in3(or_3_out), .in4(or_4_out), .in5(or_5_out), .in6(Next9),
    .in7(or_6_out), .in8(mul_code), .in9(mulu_code), .in10(or_7_out), .out(priority_encoder_1_out),
    .en_in(or_8_out));  // open: in11, in12, in13, in14, in15, gs, en_out
  or or_8 (or_8_out, or_1_out, Next2, Next9, mulu_code, mul_code, or_7_out, or_6_out, or_5_out, or_4_out, or_3_out, or_2_out);
  Multiplexer #(.width(4)) multiplexer_1 (
    .in0(4'b0000), .in1(priority_encoder_1_out), .out(OpCode), .sel(or_8_out));  // open: en
  and and_9 (Next9, NxtIns, \nor );
  and and_10 (Next10, NxtIns, \xor );
  and and_11 (Push_2, NxtIns, push);
  and and_12 (EnRM1, NxtIns, pop);
  and and_13 (Next13, NxtIns, slt);
  and and_14 (Next14, NxtIns, sltu);
  and and_15 (Next15, NxtIns, jr);
  and and_16 (Next16, NxtIns, mfhi);
  or or_9 (EnRM, EnRM2, EnRM1);
  or or_10 (EnWM, EnWM2, EnWM1);
  or or_11 (R_W, add_code1, Next2, mul_code, mulu_code, Sign, div_code2, and_code1, Next8, Next9, Next10, Pop_2, Next13, Next14, Next16, Next17, EnKbd, EnRnd, EnTTY, add_code2, and_code2, Next24, Next25, Next26, Next27, lw);
  and and_17 (Next17, NxtIns, mflo);
  and and_18 (EnKbd, NxtIns, kbd);
  and and_19 (EnRnd, NxtIns, rnd);
  and and_20 (EnTTY, NxtIns, tty);
  and and_21 (Next21, NxtIns, j);
  and and_22 (add_code2, NxtIns, addi);
  and and_23 (and_code2, NxtIns, andi);
  and and_24 (Next24, NxtIns, ori);
  or or_12 (Next, add_code1, Next2, mul_code, mulu_code, Sign, div_code2, and_code1, Next8, Next9, Next10, Next13, Next14, Next15, Next16, Next17, EnKbd, EnRnd, EnTTY, Next21, add_code2, and_code2, Next24, Next25, Next26, Next27, Next30, Next31, Next32, Next33, Next34, Stop, Next36);
  and and_25 (Next25, NxtIns, xori);
  and and_26 (Next26, NxtIns, slti);
  and and_27 (Next27, NxtIns, sltiu);
  and and_28 (EnRM2, NxtIns, lw);
  and and_29 (EnWM2, NxtIns, sw);
  and and_30 (Next30, NxtIns, beq);
  and and_31 (Next31, NxtIns, bne);
  and and_32 (Next32, NxtIns, blez);
  and and_33 (Pop_2, Mem_Ready, pop);
  and and_34 (and_34_out, ~EnWM1, Push_2);  // AND_Gate
  or or_13 (EnableSP, Pop_2, Push_2);
  and and_35 (Next33, NxtIns, bgtz);
  and and_36 (Next34, NxtIns, bltz);
  and and_37 (Stop, NxtIns, halt);
  and and_38 (Next36, NxtIns, nop);
  D_Flip_Flop d_ff_1 (.clk(Clock), .D(and_34_out), .Q(EnWM1));  // open: Qn, preset, en, reset
  or or_14 (EnInstruction, Mem_Ready, Instr_Ready);
  and and_39 (NxtIns, EnInstruction, ~Mem_Ready);  // AND_Gate

  assign beq_2 = beq;
  assign bgtz_2 = bgtz;
  assign blez_2 = blez;
  assign bltz_2 = bltz;
  assign bne_2 = bne;
  assign jump = j;
  assign jump_register = jr;

  // Other names for the same wires on the sheet: Next1 = add_code1; R_W0 = add_code1; Next22 = add_code2;
  //   R_W18 = add_code2; Next7 = and_code1; R_W6 = and_code1; Next23 = and_code2; R_W19 = and_code2; CLK = Clock;
  //   div_code1 = Sign; Next5 = Sign; R_W4 = Sign; Next6 = div_code2; R_W5 = div_code2; EnSP = EnableSP;
  //   InstEn = EnInstruction; InstR = Instr_Ready; jmp = j; MemR = Mem_Ready; Next3 = mul_code; R_W2 = mul_code;
  //   Next4 = mulu_code; R_W3 = mulu_code; Next11 = EnWM1; Next12 = EnRM1; Next28 = EnRM2; Next29 = EnWM2;
  //   Next35 = Stop; nor_code = Next9; R_W8 = Next9; Op_Code[3:0] = OpCode; or_code1 = Next8; R_W7 = Next8;
  //   or_code2 = Next24; R_W20 = Next24; EnSP2 = Push_2; PushCont = Push_2; PushRF = Push_2; EnSP1 = Pop_2;
  //   PopRF = Pop_2; R_W10 = Pop_2; R_W13 = Next16; R_W14 = Next17; Next18 = EnKbd; R_W15 = EnKbd; Next19 = EnRnd;
  //   R_W16 = EnRnd; Next20 = EnTTY; R_W17 = EnTTY; R_W24 = lw; R_W11 = Next13; slt_code1 = Next13; R_W22 = Next26;
  //   slt_code2 = Next26; R_W12 = Next14; sltu_code1 = Next14; R_W23 = Next27; sltu_code2 = Next27; R_W1 = Next2;
  //   sub_code = Next2; R_W9 = Next10; xor_code1 = Next10; R_W21 = Next25; xor_code2 = Next25

  // Notes on the sheet:
  //   Output
endmodule

module Register_File (
  input  Enable_H_L,
  input  [31:0] High,
  input  R_W,
  input  [31:0] Low,
  input  [4:0] DA,
  input  [4:0] Register_Selector_01,
  input  [4:0] Register_Selector_02,
  input  Clock,
  input  Reset,
  input  Pop,
  input  Push,
  input  EnSP,
  input  [31:0] Data,
  output [31:0] High_2,
  output [31:0] Register_01,
  output [31:0] Register_02,
  output [31:0] Low_2,
  output [31:0] Register_SP
);

  wire CH, D0, D1, D2, D3, D4, D5, D6, D7, D8, D9, D10, D11, D12, D13, D14, D15, D16, D17, D18, D19, D20,
       D21, D22, D23, D24, D25, D26, D27, D28, D29, D30, DSP, En_SP;
  wire [1:1] not_1_out;
  wire [31:0] adder_1_out, D_SP, R0, R1, R2, R3, R4, R5, R6, R7, R8, R9, R10, R11, R12, R13, R14, R15, R16,
       R17, R18, R19, R20, R21, R22, R23, R24, R25, R26, R27, R28, R29, R30, subtractor_1_out;

  Demultiplexer #(.select(5)) demultiplexer_1 (
    .out0(D0), .out1(D1), .out2(D2), .out3(D3), .out4(D4), .out5(D5), .out6(D6), .out7(D7), .out8(D8),
    .out9(D9), .out10(D10), .out11(D11), .out12(D12), .out13(D13), .out14(D14), .out15(D15), .out16(D16),
    .out17(D17), .out18(D18), .out19(D19), .out20(D20), .out21(D21), .out22(D22), .out23(D23), .out24(D24),
    .out25(D25), .out26(D26), .out27(D27), .out28(D28), .out29(D29), .out30(D30), .out31(DSP), .in(R_W),
    .sel(DA));  // open: en
  Register #(.width(32)) u_R0 (.D({32{1'b0}}), .en(D0), .Q(R0), .clk(Clock), .clr(Reset));
  Register #(.width(32)) u_R8 (.D(Data), .en(D8), .Q(R8), .clk(Clock), .clr(Reset));
  Register #(.width(32)) u_R16 (.D(Data), .en(D16), .Q(R16), .clk(Clock), .clr(Reset));
  Register #(.width(32)) u_R24 (.D(Data), .en(D24), .Q(R24), .clk(Clock), .clr(Reset));
  Multiplexer #(.select(5), .width(32)) multiplexer_1 (
    .in0(R0), .in1(R1), .in2(R2), .in3(R3), .in4(R4), .in5(R5), .in6(R6), .in7(R7), .in8(R8), .in9(R9),
    .in10(R10), .in11(R11), .in12(R12), .in13(R13), .in14(R14), .in15(R15), .in16(R16), .in17(R17),
    .in18(R18), .in19(R19), .in20(R20), .in21(R21), .in22(R22), .in23(R23), .in24(R24), .in25(R25),
    .in26(R26), .in27(R27), .in28(R28), .in29(R29), .in30(R30), .in31(Register_SP), .out(Register_01),
    .sel(Register_Selector_01));  // open: en
  Register #(.width(32)) u_R1 (.D(Data), .en(D1), .Q(R1), .clk(Clock), .clr(Reset));
  Register #(.width(32)) u_R9 (.D(Data), .en(D9), .Q(R9), .clk(Clock), .clr(Reset));
  Register #(.width(32)) u_R17 (.D(Data), .en(D17), .Q(R17), .clk(Clock), .clr(Reset));
  Register #(.width(32)) u_R25 (.D(Data), .en(D25), .Q(R25), .clk(Clock), .clr(Reset));
  Multiplexer #(.select(5), .width(32)) multiplexer_2 (
    .in0(R0), .in1(R1), .in2(R2), .in3(R3), .in4(R4), .in5(R5), .in6(R6), .in7(R7), .in8(R8), .in9(R9),
    .in10(R10), .in11(R11), .in12(R12), .in13(R13), .in14(R14), .in15(R15), .in16(R16), .in17(R17),
    .in18(R18), .in19(R19), .in20(R20), .in21(R21), .in22(R22), .in23(R23), .in24(R24), .in25(R25),
    .in26(R26), .in27(R27), .in28(R28), .in29(R29), .in30(R30), .in31(Register_SP), .out(Register_02),
    .sel(Register_Selector_02));  // open: en
  Register #(.width(32)) u_R2 (.D(Data), .en(D2), .Q(R2), .clk(Clock), .clr(Reset));
  Register #(.width(32)) u_R10 (.D(Data), .en(D10), .Q(R10), .clk(Clock), .clr(Reset));
  Register #(.width(32)) u_R18 (.D(Data), .en(D18), .Q(R18), .clk(Clock), .clr(Reset));
  Register #(.width(32)) u_R26 (.D(Data), .en(D26), .Q(R26), .clk(Clock), .clr(Reset));
  Register #(.width(32)) u_R3 (.D(Data), .en(D3), .Q(R3), .clk(Clock), .clr(Reset));
  Register #(.width(32)) u_R11 (.D(Data), .en(D11), .Q(R11), .clk(Clock), .clr(Reset));
  Register #(.width(32)) u_R19 (.D(Data), .en(D19), .Q(R19), .clk(Clock), .clr(Reset));
  Register #(.width(32)) u_R27 (.D(Data), .en(D27), .Q(R27), .clk(Clock), .clr(Reset));
  Register #(.width(32)) u_R4 (.D(Data), .en(D4), .Q(R4), .clk(Clock), .clr(Reset));
  Register #(.width(32)) Hi (.D(High), .en(Enable_H_L), .Q(High_2), .clk(Clock), .clr(Reset));
  Register #(.width(32)) Lo (.D(Low), .en(Enable_H_L), .Q(Low_2), .clk(Clock), .clr(Reset));
  Register #(.width(32)) u_R12 (.D(Data), .en(D12), .Q(R12), .clk(Clock), .clr(Reset));
  Register #(.width(32)) u_R20 (.D(Data), .en(D20), .Q(R20), .clk(Clock), .clr(Reset));
  Register #(.width(32)) u_R28 (.D(Data), .en(D28), .Q(R28), .clk(Clock), .clr(Reset));
  Register #(.width(32)) u_R5 (.D(Data), .en(D5), .Q(R5), .clk(Clock), .clr(Reset));
  Register #(.width(32)) u_R13 (.D(Data), .en(D13), .Q(R13), .clk(Clock), .clr(Reset));
  Register #(.width(32)) u_R21 (.D(Data), .en(D21), .Q(R21), .clk(Clock), .clr(Reset));
  Register #(.width(32)) u_R29 (.D(Data), .en(D29), .Q(R29), .clk(Clock), .clr(Reset));
  Register #(.width(32)) u_R6 (.D(Data), .en(D6), .Q(R6), .clk(Clock), .clr(Reset));
  Adder #(.width(32)) adder_1 (.a(Register_SP), .b(32'h4), .out(adder_1_out));  // open: cin, cout
  not not_1 (not_1_out[1], CH);
  Subtractor #(.width(32)) subtractor_1 (.a(Register_SP), .b(32'h4), .out(subtractor_1_out));  // open: bin, bout
  or or_1 (CH, Push, Pop);
  or or_2 (En_SP, DSP, EnSP);
  Register #(.width(32)) u_R14 (.D(Data), .en(D14), .Q(R14), .clk(Clock), .clr(Reset));
  Register #(.width(32)) u_R22 (.D(Data), .en(D22), .Q(R22), .clk(Clock), .clr(Reset));
  Register #(.width(32)) u_R30 (.D(Data), .en(D30), .Q(R30), .clk(Clock), .clr(Reset));
  Multiplexer #(.select(2), .width(32)) multiplexer_3 (
    .in0(adder_1_out), .in1(subtractor_1_out), .out(D_SP), .sel({not_1_out[1], Push}));  // open: in2, in3, en
  Register #(.width(32)) u_R7 (.D(Data), .en(D7), .Q(R7), .clk(Clock), .clr(Reset));
  Register #(.width(32)) u_R15 (.D(Data), .en(D15), .Q(R15), .clk(Clock), .clr(Reset));
  Register #(.width(32)) u_R23 (.D(Data), .en(D23), .Q(R23), .clk(Clock), .clr(Reset));
  Register #(.width(32)) RSP (.D(D_SP), .en(En_SP), .Q(Register_SP), .clk(Clock), .clr(Reset));

  // Other names for the same wires on the sheet: CLK = Clock; D[31:0] = Data; RS1[4:0] = Register_Selector_01;
  //   RS2[4:0] = Register_Selector_02; RSP[31:0] = Register_SP; RST = Reset

  // Notes on the sheet:
  //   Direction Addres
  //   Output
  //   RegisterFile
endmodule

module ALU (
  input  [31:0] X,
  input  [31:0] Y,
  input  [3:0] OP_Code,
  input  Sign,
  output [31:0] Result,
  output SF,
  output ZF,
  output Eq,
  output Ne,
  output Lez,
  output [31:0] High,
  output [31:0] Low,
  output Gtz,
  output Ltz
);

  wire [0:0] Sltu;
  wire [31:0] Add, And, DivHi, DivLo, DivuHi, DivuLo, MultHi, MultLo, MuluHi, MuluLo, Nor, Or, Sub, Xor;

  Adder #(.width(32)) adder_1 (.a(X), .b(Y), .out(Add));  // open: cin, cout
  Subtractor #(.width(32)) subtractor_1 (.a(X), .b(Y), .out(Sub));  // open: bin, bout
  Comparator #(.width(32), .mode("unsigned")) comparator_1 (.a(X), .b(Y), .lt(Sltu[0]));  // open: gt, eq
  Multiplier #(.width(32)) multiplier_1 (.a(X), .b(Y), .out(MultLo), .cout(MultHi));  // open: cin
  Divider #(.width(32)) divider_1 (.a(X), .b(Y), .out(DivuHi), .rem(DivuLo));  // open: upper
  assign And = X & Y;  // AND_Gate and_1, 32 bits wide
  Multiplexer #(.select(2), .width(32)) multiplexer_1 (
    .in0(MultHi), .in1(MuluHi), .in2(DivHi), .out(High), .sel(OP_Code[1:0]), .en(OP_Code[3]));  // open: in3
  Multiplexer #(.select(2), .width(32)) multiplexer_2 (
    .in0(MultLo), .in1(MuluLo), .in2(DivLo), .out(Low), .sel(OP_Code[1:0]), .en(OP_Code[3]));  // open: in3
  assign Or = X | Y;  // OR_Gate or_1, 32 bits wide
  assign Nor = ~(X | Y);  // NOR_Gate nor_1, 32 bits wide
  assign Xor = X ^ Y;  // XOR_Gate xor_1, 32 bits wide
  Mulu mulu_1 (.X(X), .Y(Y), .Low(MuluLo), .High(MuluHi));
  Div div_1 (.X(X), .Y(Y), .Cociente(DivLo), .Resto(DivHi), .Sign(Sign));
  Comparator #(.width(32)) comparator_2 (.a(X), .b(Y), .gt(Gtz), .eq(Eq), .lt(Ltz));
  or or_2 (Lez, Ltz, Eq);
  Multiplexer #(.select(4), .width(32)) multiplexer_3 (
    .in0(Add), .in1(Sub), .in2({{31{1'b0}}, Ltz}), .in3({{31{1'b0}}, Sltu[0]}), .in4(And), .in5(Or),
    .in6(Nor), .in7(Xor), .in8(MultLo), .in9(MuluLo), .in10(DivHi), .out(Result), .sel(OP_Code));  // open: in11, in12, in13, in14, in15, en
  not not_1 (Ne, Eq);
  Comparator #(.width(32)) comparator_3 (.a(Result), .b({32{1'b0}}), .eq(ZF));  // open: gt, lt

  assign SF = Result[0];

  // Other names for the same wires on the sheet: Mul_Div[1:0] = OP_Code[1:0]; OpCod[3:0] = OP_Code;
  //   EnMul_Div = OP_Code[3]; Sgn = Sign; Slt[0] = Ltz

  // Notes on the sheet:
  //   ALU
endmodule

module Mulu (
  input  [31:0] X,
  input  [31:0] Y,
  output [31:0] Low,
  output [31:0] High
);

  wire Carry_2, Carry_3, Carry_4_t, not_1_out, not_2_out;
  wire [0:0] and_1_out;
  wire [31:0] adder_1_out, adder_2_out, adder_4_out, adder_5_out, Carry, shifter_1_out, shifter_4_out, X_2,
       X___1, Y_2, Y___1;
  wire [31:2] Result;
  wire [31:30] Carry_4;

  Shifter #(.width(32)) shifter_1 (.in(X_2), .\dist (5'b00001), .out(shifter_1_out));
  assign X___1 = Y[0] ? shifter_1_out : 32'bz;  // Controlled_Buffer controlled_buffer_1
  assign X___1 = not_1_out ? {32{1'b0}} : 32'bz;  // Controlled_Buffer controlled_buffer_2
  not not_1 (not_1_out, Y[0]);
  Shifter #(.width(32), .shift("lr")) shifter_2 (.in(X), .\dist (5'b00001), .out(X_2));
  Shifter #(.width(32), .shift("lr")) shifter_3 (.in(Y), .\dist (5'b00001), .out(Y_2));
  assign Y___1 = X[0] ? shifter_4_out : 32'bz;  // Controlled_Buffer controlled_buffer_3
  Shifter #(.width(32)) shifter_4 (.in(Y_2), .\dist (5'b00001), .out(shifter_4_out));
  assign Y___1 = not_2_out ? {32{1'b0}} : 32'bz;  // Controlled_Buffer controlled_buffer_4
  not not_2 (not_2_out, X[0]);
  Multiplier #(.width(32)) multiplier_1 (
    .a(X_2), .b(Y_2), .out({Carry[1:0], Result}), .cout({Carry_4, Carry[31:2]}));  // open: cin
  and and_1 (and_1_out[0], Y[0], X[0]);
  Adder #(.width(32)) adder_1 (.a(X___1), .b(Y___1), .out(adder_1_out), .cout(Carry_2));  // open: cin
  Adder #(.width(32)) adder_2 (
    .a({{31{1'b0}}, Carry_2}), .b({{31{1'b0}}, Carry_3}), .out(adder_2_out));  // open: cin, cout
  Adder #(.width(32)) adder_3 (.a({Result, 2'b00}), .b(adder_4_out), .out(Low), .cout(Carry_4_t));  // open: cin
  Adder #(.width(32)) adder_4 (
    .a(adder_1_out), .b({{31{1'b0}}, and_1_out[0]}), .out(adder_4_out), .cout(Carry_3));  // open: cin
  Adder #(.width(32)) adder_5 (.a(adder_2_out), .b({{31{1'b0}}, Carry_4_t}), .out(adder_5_out));  // open: cin, cout
  Adder #(.width(32)) adder_6 (.a(adder_5_out), .b(Carry), .out(High));  // open: cin, cout

  // Other names for the same wires on the sheet: Result_4[31:0] = {Carry[1:0], Result}; Carry_4[29:0] = Carry[31:2];
  //   X_0 = X[0]; Y_0 = Y[0]

  // Notes on the sheet:
  //   MULU
endmodule

module Div (
  input  Sign,
  input  [31:0] X,
  input  [31:0] Y,
  output [31:0] Cociente,
  output [31:0] Resto
);

  wire and_1_out, and_2_out, C2;
  wire [31:0] divider_1_out, minus_X, minus_Y, multiplexer_1_out, multiplexer_2_out, negator_3_out;

  Negator #(.width(32)) negator_1 (.in(X), .out(minus_X));
  Negator #(.width(32)) negator_2 (.in(Y), .out(minus_Y));
  Multiplexer #(.width(32), .enable("false")) multiplexer_1 (
    .in0(X), .in1(minus_X), .out(multiplexer_1_out), .sel(and_1_out));
  and and_1 (and_1_out, X[31], Sign);
  Multiplexer #(.width(32), .enable("false")) multiplexer_2 (
    .in0(Y), .in1(minus_Y), .out(multiplexer_2_out), .sel(and_2_out));
  and and_2 (and_2_out, Sign, Y[31]);
  Divider #(.width(32)) divider_1 (
    .a(multiplexer_1_out), .b(multiplexer_2_out), .out(divider_1_out), .rem(Resto));  // open: upper
  xor xor_1 (C2, X[31], Y[31]);
  Multiplexer #(.width(32), .enable("false")) multiplexer_3 (
    .in0(divider_1_out), .in1(negator_3_out), .out(Cociente), .sel(C2));
  Negator #(.width(32)) negator_3 (.in(divider_1_out), .out(negator_3_out));

  // Other names for the same wires on the sheet: Sgn = Sign; SgnX = X[31]; SgnY = Y[31]
endmodule

module Instruction_Decoder (
  input  [31:0] in_1,
  output nop,
  output addi,
  output pop,
  output divu,
  output add,
  output sltiu,
  output slti,
  output push,
  output slt,
  output sub,
  output ori,
  output andi,
  output halt,
  output sltu,
  output mult,
  output lw,
  output xori,
  output rnd,
  output tty,
  output \and ,
  output mulu,
  output bq,
  output sw,
  output kbd,
  output \or ,
  output div,
  output bne,
  output blez,
  output jump,
  output \nor ,
  output \xor ,
  output bltz,
  output bgtz,
  output [4:0] Rd,
  output [4:0] Rt,
  output mhfi,
  output [4:0] Rs,
  output jr,
  output [4:0] X,
  output [25:0] Destino_Salto,
  output mflo,
  output [31:0] Constante_A2
);

  wire or_1_out, R1, R2, R3;

  and and_1 (R1, ~in_1[26], ~in_1[27], ~in_1[28], ~in_1[29], ~in_1[30], ~in_1[31]);  // AND_Gate
  and and_2 (R2, ~in_1[26], ~in_1[27], ~in_1[28], in_1[29], in_1[30], in_1[31]);  // AND_Gate
  and and_3 (R3, in_1[26], in_1[27], in_1[28], in_1[29], in_1[30], in_1[31]);
  and and_4 (jump, ~in_1[26], in_1[27], ~in_1[28], ~in_1[29], ~in_1[30], ~in_1[31]);  // AND_Gate
  and and_5 (divu, R1, in_1[0], in_1[1], ~in_1[2], in_1[3], in_1[4], ~in_1[5]);  // AND_Gate
  and and_6 (slt, R1, ~in_1[0], in_1[1], ~in_1[2], in_1[3], ~in_1[4], in_1[5]);  // AND_Gate
  and and_7 (sltu, R1, in_1[0], in_1[1], ~in_1[2], in_1[3], ~in_1[4], in_1[5]);  // AND_Gate
  and and_8 (\and , R1, ~in_1[0], ~in_1[1], in_1[2], ~in_1[3], ~in_1[4], in_1[5]);  // AND_Gate
  and and_9 (\or , R1, in_1[0], ~in_1[1], in_1[2], ~in_1[3], ~in_1[4], in_1[5]);  // AND_Gate
  and and_10 (\nor , R1, in_1[0], in_1[1], in_1[2], ~in_1[3], ~in_1[4], in_1[5]);  // AND_Gate
  and and_11 (mhfi, R1, ~in_1[0], ~in_1[1], ~in_1[2], ~in_1[3], in_1[4], ~in_1[5]);  // AND_Gate
  and and_12 (mflo, R1, ~in_1[0], in_1[1], ~in_1[2], ~in_1[3], in_1[4], ~in_1[5]);  // AND_Gate
  and and_13 (nop, ~in_1[0], ~in_1[1], ~in_1[2], ~in_1[3], ~in_1[4], ~in_1[5], R1);  // AND_Gate
  and and_14 (add, ~in_1[0], ~in_1[1], ~in_1[2], ~in_1[3], ~in_1[4], in_1[5], R1);  // AND_Gate
  and and_15 (sub, ~in_1[0], in_1[1], ~in_1[2], ~in_1[3], ~in_1[4], in_1[5], R1);  // AND_Gate
  and and_16 (mult, ~in_1[0], ~in_1[1], ~in_1[2], in_1[3], in_1[4], ~in_1[5], R1);  // AND_Gate
  and and_17 (mulu, in_1[0], ~in_1[1], ~in_1[2], in_1[3], in_1[4], ~in_1[5], R1);  // AND_Gate
  and and_18 (div, ~in_1[0], in_1[1], ~in_1[2], in_1[3], in_1[4], ~in_1[5], R1);  // AND_Gate
  and and_19 (\xor , ~in_1[0], ~in_1[1], ~in_1[2], in_1[3], ~in_1[4], in_1[5], R1);  // AND_Gate
  and and_20 (jr, ~in_1[0], ~in_1[1], ~in_1[2], in_1[3], ~in_1[4], ~in_1[5], R1);  // AND_Gate
  and and_21 (sltiu, in_1[26], in_1[27], ~in_1[28], in_1[29], ~in_1[30], ~in_1[31]);  // AND_Gate
  and and_22 (ori, in_1[26], ~in_1[27], in_1[28], in_1[29], ~in_1[30], ~in_1[31]);  // AND_Gate
  and and_23 (lw, in_1[26], in_1[27], ~in_1[28], ~in_1[29], ~in_1[30], in_1[31]);  // AND_Gate
  and and_24 (bq, ~in_1[26], ~in_1[27], in_1[28], ~in_1[29], ~in_1[30], ~in_1[31]);  // AND_Gate
  and and_25 (bne, in_1[26], ~in_1[27], in_1[28], ~in_1[29], ~in_1[30], ~in_1[31]);  // AND_Gate
  and and_26 (bltz, in_1[26], ~in_1[27], ~in_1[28], ~in_1[29], ~in_1[30], ~in_1[31]);  // AND_Gate
  and and_27 (addi, ~in_1[26], ~in_1[27], ~in_1[28], in_1[29], ~in_1[30], ~in_1[31]);  // AND_Gate
  and and_28 (slti, ~in_1[26], in_1[27], ~in_1[28], in_1[29], ~in_1[30], ~in_1[31]);  // AND_Gate
  and and_29 (andi, ~in_1[26], ~in_1[27], in_1[28], in_1[29], ~in_1[30], ~in_1[31]);  // AND_Gate
  and and_30 (xori, ~in_1[26], in_1[27], in_1[28], in_1[29], ~in_1[30], ~in_1[31]);  // AND_Gate
  and and_31 (sw, in_1[26], in_1[27], ~in_1[28], in_1[29], ~in_1[30], in_1[31]);  // AND_Gate
  and and_32 (blez, ~in_1[26], in_1[27], in_1[28], ~in_1[29], ~in_1[30], ~in_1[31]);  // AND_Gate
  and and_33 (bgtz, in_1[26], in_1[27], in_1[28], ~in_1[29], ~in_1[30], ~in_1[31]);  // AND_Gate
  Multiplexer #(.width(32)) multiplexer_1 (
    .in0({{17{in_1[15]}}, in_1[14:0]}), .in1({{16{1'b0}}, in_1[15:0]}), .out(Constante_A2), .sel(or_1_out));  // open: en
  or or_1 (or_1_out, andi, ori, xori);
  and and_34 (rnd, R3, ~in_1[0], in_1[1], ~in_1[2], ~in_1[3], ~in_1[4], ~in_1[5]);  // AND_Gate
  and and_35 (kbd, R3, ~in_1[0], ~in_1[1], in_1[2], ~in_1[3], ~in_1[4], ~in_1[5]);  // AND_Gate
  and and_36 (push, R2, ~in_1[5], ~in_1[4], ~in_1[3], ~in_1[2], ~in_1[1], in_1[0]);  // AND_Gate
  and and_37 (pop, ~in_1[0], ~in_1[1], ~in_1[2], ~in_1[3], ~in_1[4], ~in_1[5], R2);  // AND_Gate
  and and_38 (halt, in_1[0], in_1[1], in_1[2], in_1[3], in_1[4], in_1[5], R3);
  and and_39 (tty, in_1[0], ~in_1[1], ~in_1[2], ~in_1[3], ~in_1[4], ~in_1[5], R3);  // AND_Gate

  assign Destino_Salto = in_1[25:0];
  assign Rd = in_1[15:11];
  assign Rs = in_1[25:21];
  assign Rt = in_1[20:16];
  assign X = in_1[10:6];

  // Other names for the same wires on the sheet: Func_code[5:0] = in_1[5:0]; Op_code[5:0] = in_1[31:26]

  // Notes on the sheet:
  //   Instruction
endmodule

module Program_Counter (
  input  [31:0] PC_In,
  input  Enable,
  input  Clock,
  input  Clear,
  output [31:0] PC_Out
);

  Register #(.width(32)) register_1 (.D(PC_In), .en(Enable), .Q(PC_Out), .clk(Clock), .clr(Clear));

  // Notes on the sheet:
  //   Program Counter
endmodule

module Branch_Control (
  input  Beq,
  input  Eq,
  input  Bne,
  input  Ne,
  input  Blez,
  input  Next_Inst,
  input  Lez,
  input  Bgtz,
  input  Gtz,
  input  Bltz,
  input  Jump,
  input  Jmp_Re,
  input  Ltz,
  input  [31:0] PC_In,
  input  [31:0] RS,
  input  [25:0] Destino_Salto,
  input  [31:0] Offset,
  output [31:0] PC_Out
);

  wire and_1_out, and_2_out, and_3_out, and_4_out, and_5_out, Branch_Inst;
  wire [1:0] or_3_out;
  wire [31:0] Branch, multiplexer_1_out, PC___4, shifter_1_out;

  and and_1 (and_1_out, Beq, Eq);
  and and_2 (and_2_out, Bne, Ne);
  and and_3 (and_3_out, Blez, Lez);
  and and_4 (and_4_out, Bgtz, Gtz);
  and and_5 (and_5_out, Bltz, Ltz);
  or or_1 (Branch_Inst, and_1_out, and_2_out, and_3_out, and_4_out, and_5_out);
  or or_2 (or_3_out[1], Jmp_Re, Branch_Inst);
  Multiplexer #(.select(2), .width(32)) multiplexer_1 (
    .in0(PC___4), .in1({PC_In[31:28], Destino_Salto, 2'b00}), .in2(RS), .in3(Branch),
    .out(multiplexer_1_out), .sel(or_3_out));  // open: en
  or or_3 (or_3_out[0], Branch_Inst, Jump);
  Multiplexer #(.width(32)) multiplexer_2 (
    .in0(PC_In), .in1(multiplexer_1_out), .out(PC_Out), .sel(Next_Inst));  // open: en
  Shifter #(.width(32)) shifter_1 (.in(Offset), .\dist (5'b00010), .out(shifter_1_out));
  Adder #(.width(32)) adder_1 (.a(32'h4), .b(PC_In), .out(PC___4));  // open: cin, cout
  Adder #(.width(32)) adder_2 (.a(PC___4), .b(shifter_1_out), .out(Branch));  // open: cin, cout

  // Other names for the same wires on the sheet: jmp = Jump; jr = Jmp_Re; Dest[25:0] = Destino_Salto;
  //   Jump_To[31:2] = {PC_In[31:28], Destino_Salto}

  // Notes on the sheet:
  //   Branch Control
endmodule

module Write_Memory (
  input  [31:0] Data,
  input  [31:0] Direction,
  input  Clock,
  input  Enable,
  input  Reset,
  input  [3:0] Write_Time,
  output [3:0] Mask,
  output [31:0] Ram_1,
  output [15:0] Address,
  output [31:0] Ram_2,
  output [31:0] Ram_3,
  output Finish,
  output [31:0] Ram_4,
  output CS
);

  wire [31:0] register_1_q;

  Waiting_Cycles waiting_cycles_1 (
    .Read_Time(Write_Time), .clk(Clock), .Start(Enable), .Reset(Reset), .Finish(Finish), .Chip_Select(CS));
  Decoder #(.select(2)) decoder_1 (
    .out0(Mask[0]), .out1(Mask[1]), .out2(Mask[2]), .out3(Mask[3]), .sel(Direction[3:2]));  // open: en
  Register #(.width(32)) register_1 (
    .D({Data[7:0], Data[15:8], Data[23:16], Data[31:24]}), .en(CS), .Q(register_1_q), .clk(Clock), .clr(Reset));
  Demultiplexer #(.select(2), .width(32)) demultiplexer_1 (
    .out0(Ram_1), .out1(Ram_2), .out2(Ram_3), .out3(Ram_4), .in(register_1_q), .sel(Direction[3:2]));  // open: en

  assign Address = Direction[19:4];

  // Other names for the same wires on the sheet: dat[31:0] = Data; clk = Clock; Bank[1:0] = Direction[3:2];
  //   en = Enable; rst = Reset; wt[3:0] = Write_Time

  // Notes on the sheet:
  //   Write Memory
endmodule

module Read_Memory (
  input  [31:0] Ram_1,
  input  Clock,
  input  Enable,
  input  [31:0] Ram_2,
  input  Reset,
  input  [3:0] Read_Time,
  input  [31:0] Ram_3,
  input  [31:0] Ram_4,
  input  [31:0] Address_In,
  output Finish,
  output Chip_Select,
  output [31:0] Ram_Out,
  output [15:0] Address_Out
);

  wire waiting_cycles_1_finish;
  wire [31:0] multiplexer_1_out;

  Multiplexer #(.select(2), .width(32)) multiplexer_1 (
    .in0(Ram_1), .in1(Ram_2), .in2(Ram_3), .in3(Ram_4), .out(multiplexer_1_out), .sel(Address_In[3:2]));  // open: en
  Register #(.width(32)) register_1 (
    .D({multiplexer_1_out[7:0], multiplexer_1_out[15:8], multiplexer_1_out[23:16], multiplexer_1_out[31:24]}),
    .en(Chip_Select), .Q(Ram_Out), .clk(Clock), .clr(Reset));
  Waiting_Cycles waiting_cycles_1 (
    .Read_Time(Read_Time), .clk(Clock), .Start(Enable), .Reset(Reset), .Finish(waiting_cycles_1_finish),
    .Chip_Select(Chip_Select));
  D_Flip_Flop d_ff_1 (.clk(Clock), .D(waiting_cycles_1_finish), .Q(Finish));  // open: Qn, preset, en, reset

  assign Address_Out = Address_In[19:4];

  // Other names for the same wires on the sheet: clk = Clock; cs = Chip_Select; en = Enable; rst = Reset;
  //   rt[3:0] = Read_Time

  // Notes on the sheet:
  //   Read Memory
endmodule

module Instruction_Fetcher (
  input  [31:0] Ram_1,
  input  Clock,
  input  Enable,
  input  [31:0] Ram_2,
  input  Reset,
  input  [31:0] Ram_3,
  input  [31:0] Ram_4,
  input  [31:0] PC,
  output Finish,
  output [31:0] Instruction
);

  wire [31:0] multiplexer_1_out;

  Multiplexer #(.select(2), .width(32)) multiplexer_1 (
    .in0(Ram_1), .in1(Ram_2), .in2(Ram_3), .in3(Ram_4), .out(multiplexer_1_out), .sel(PC[3:2]));  // open: en
  Register #(.width(32)) register_1 (
    .D({multiplexer_1_out[7:0], multiplexer_1_out[15:8], multiplexer_1_out[23:16], multiplexer_1_out[31:24]}),
    .en(Enable), .Q(Instruction), .clk(Clock), .clr(Reset));
  D_Flip_Flop d_ff_1 (.clk(Clock), .D(Enable), .Q(Finish));  // open: Qn, preset, en, reset

  // Other names for the same wires on the sheet: clk = Clock; en = Enable; rst = Reset

  // Notes on the sheet:
  //   Instruction Fetcher
endmodule

module Waiting_Cycles (
  input  [3:0] Read_Time,
  input  clk,
  input  Start,
  input  Reset,
  output Finish,
  output Chip_Select
);

  wire comparator_1_eq, CS1, d_ff_1_q, or_2_out;
  wire [3:0] counter_1_q;

  or or_1 (Chip_Select, CS1, Finish);
  or or_2 (or_2_out, CS1, Start);
  D_Flip_Flop d_ff_1 (.clk(clk), .D(or_2_out), .Q(d_ff_1_q));  // open: Qn, preset, en, reset
  Demultiplexer demultiplexer_1 (.out0(CS1), .out1(Finish), .in(d_ff_1_q), .sel(comparator_1_eq));  // open: en
  Counter #(.width(4), .max('hf)) counter_1 (
    .load(or_2_out), .D(Read_Time), .count(CS1), .Q(counter_1_q), .clk(clk));  // open: carry, clr
  Comparator #(.width(4)) comparator_1 (.a(counter_1_q), .b(4'b0000), .eq(comparator_1_eq));  // open: gt, lt

  // Other names for the same wires on the sheet: CS2 = Finish; rst = Reset; rt[3:0] = Read_Time; str = Start

  // Notes on the sheet:
  //   Waiting Cycles
endmodule

module Instruction_Cache (
  input  Clock,
  input  [31:0] Ram_0,
  input  Enable,
  input  Reset,
  input  [3:0] Read_Time,
  input  [31:0] Ram_1,
  input  Dirty,
  input  [31:0] Ram_2,
  input  [31:0] Ram_3,
  input  [31:0] PC,
  output [31:0] Cache_Out_0,
  output [31:0] Cache_Out_1,
  output [31:0] Cache_Out_2,
  output [31:0] Cache_Out_3,
  output [15:0] Address,
  output Chip_Select,
  output Finish
);

  wire and_1_out, comparator_1_eq, controlled_buffer_1_out, controlled_buffer_2_out, controlled_buffer_3_out,
       controlled_buffer_4_out, controlled_buffer_5_out, controlled_buffer_6_out, controlled_buffer_7_out,
       controlled_buffer_8_out, d_ff_1_q, d_ff_2_q, decoder_1_out0, decoder_1_out1, decoder_1_out2,
       decoder_1_out3, decoder_1_out4, decoder_1_out5, decoder_1_out6, decoder_1_out7, demultiplexer_1_out0,
       demultiplexer_2_out0, demultiplexer_2_out1, finish_t, miss, not_2_out, not_3_out, not_4_out,
       not_5_out, not_6_out, not_7_out, not_8_out, not_9_out, or_1_out, or_2_out, ready, Sart_q, start,
       valid, valid0, valid1, valid2, valid3, valid4, valid5, valid6, valid7;
  wire [12:0] ram_5_data;

  D_Flip_Flop Sart (.clk(Clock), .D(Enable), .Q(Sart_q));  // open: Qn, preset, en, reset
  D_Flip_Flop d_ff_1 (.Q(d_ff_1_q), .preset(Dirty), .reset(finish_t));  // open: clk, D, Qn, en
  Waiting_Cycles waiting_cycles_1 (
    .Read_Time(Read_Time), .clk(Clock), .Start(start), .Reset(Reset), .Finish(finish_t),
    .Chip_Select(Chip_Select));
  Demultiplexer demultiplexer_1 (.out0(demultiplexer_1_out0), .out1(start), .in(Sart_q), .sel(or_1_out));  // open: en
  or or_1 (or_1_out, d_ff_1_q, miss);
  or or_2 (or_2_out, demultiplexer_2_out0, start);
  D_Flip_Flop d_ff_2 (.clk(Clock), .D(or_2_out), .Q(d_ff_2_q));  // open: Qn, preset, en, reset
  Demultiplexer demultiplexer_2 (
    .out0(demultiplexer_2_out0), .out1(demultiplexer_2_out1), .in(d_ff_2_q), .sel(finish_t));  // open: en
  or or_3 (ready, demultiplexer_1_out0, demultiplexer_2_out1);
  RAM_part #(.addrWidth(3), .dataWidth(32), .bus("separate")) u_ram_1 (
    .addr(PC[6:4]), .din(Ram_0), .data(Cache_Out_0), .str(finish_t), .clk(Clock), .ld(1'b1), .clr(Reset));  // open: sel
  RAM_part #(.addrWidth(3), .dataWidth(32), .bus("separate")) u_ram_2 (
    .addr(PC[6:4]), .din(Ram_1), .data(Cache_Out_1), .str(finish_t), .clk(Clock), .ld(1'b1), .clr(Reset));  // open: sel
  RAM_part #(.addrWidth(3), .dataWidth(32), .bus("separate")) u_ram_3 (
    .addr(PC[6:4]), .din(Ram_2), .data(Cache_Out_2), .str(finish_t), .clk(Clock), .ld(1'b1), .clr(Reset));  // open: sel
  RAM_part #(.addrWidth(3), .dataWidth(32), .bus("separate")) ram_4 (
    .addr(PC[6:4]), .din(Ram_3), .data(Cache_Out_3), .str(finish_t), .clk(Clock), .ld(1'b1), .clr(Reset));  // open: sel
  RAM_part #(.addrWidth(3), .dataWidth(13), .bus("separate")) ram_5 (
    .addr(PC[6:4]), .din(PC[19:7]), .data(ram_5_data), .str(finish_t), .clk(Clock), .ld(1'b1), .clr(Reset));  // open: sel
  D_Flip_Flop d_ff_3 (.clk(Clock), .D(ready), .Q(Finish));  // open: Qn, preset, en, reset
  Decoder #(.select(3)) decoder_1 (
    .out0(decoder_1_out0), .out1(decoder_1_out1), .out2(decoder_1_out2), .out3(decoder_1_out3),
    .out4(decoder_1_out4), .out5(decoder_1_out5), .out6(decoder_1_out6), .out7(decoder_1_out7), .sel(PC[6:4]));  // open: en
  Comparator #(.width(13)) comparator_1 (.a(PC[19:7]), .b(ram_5_data), .eq(comparator_1_eq));  // open: gt, lt
  and and_1 (and_1_out, valid, comparator_1_eq);
  not not_1 (miss, and_1_out);
  assign controlled_buffer_1_out = not_2_out ? decoder_1_out0 : 1'bz;  // Controlled_Buffer controlled_buffer_1
  assign controlled_buffer_2_out = not_3_out ? decoder_1_out1 : 1'bz;  // Controlled_Buffer controlled_buffer_2
  assign controlled_buffer_3_out = not_4_out ? decoder_1_out2 : 1'bz;  // Controlled_Buffer controlled_buffer_3
  assign controlled_buffer_4_out = not_5_out ? decoder_1_out3 : 1'bz;  // Controlled_Buffer controlled_buffer_4
  assign controlled_buffer_5_out = not_6_out ? decoder_1_out4 : 1'bz;  // Controlled_Buffer controlled_buffer_5
  assign controlled_buffer_6_out = not_7_out ? decoder_1_out5 : 1'bz;  // Controlled_Buffer controlled_buffer_6
  assign controlled_buffer_7_out = not_8_out ? decoder_1_out6 : 1'bz;  // Controlled_Buffer controlled_buffer_7
  assign controlled_buffer_8_out = not_9_out ? decoder_1_out7 : 1'bz;  // Controlled_Buffer controlled_buffer_8
  not not_2 (not_2_out, valid0);
  D_Flip_Flop d_ff_4 (.clk(Clock), .D(controlled_buffer_1_out), .Q(valid0), .reset(Reset));  // open: Qn, preset, en
  not not_3 (not_3_out, valid1);
  D_Flip_Flop d_ff_5 (.clk(Clock), .D(controlled_buffer_2_out), .Q(valid1), .reset(Reset));  // open: Qn, preset, en
  not not_4 (not_4_out, valid2);
  D_Flip_Flop d_ff_6 (.clk(Clock), .D(controlled_buffer_3_out), .Q(valid2), .reset(Reset));  // open: Qn, preset, en
  not not_5 (not_5_out, valid3);
  D_Flip_Flop d_ff_7 (.clk(Clock), .D(controlled_buffer_4_out), .Q(valid3), .reset(Reset));  // open: Qn, preset, en
  not not_6 (not_6_out, valid4);
  D_Flip_Flop d_ff_8 (.clk(Clock), .D(controlled_buffer_5_out), .Q(valid4), .reset(Reset));  // open: Qn, preset, en
  not not_7 (not_7_out, valid5);
  D_Flip_Flop d_ff_9 (.clk(Clock), .D(controlled_buffer_6_out), .Q(valid5), .reset(Reset));  // open: Qn, preset, en
  not not_8 (not_8_out, valid6);
  D_Flip_Flop d_ff_10 (.clk(Clock), .D(controlled_buffer_7_out), .Q(valid6), .reset(Reset));  // open: Qn, preset, en
  not not_9 (not_9_out, valid7);
  D_Flip_Flop d_ff_11 (.clk(Clock), .D(controlled_buffer_8_out), .Q(valid7), .reset(Reset));  // open: Qn, preset, en
  Multiplexer #(.select(3)) multiplexer_1 (
    .in0(valid0), .in1(valid1), .in2(valid2), .in3(valid3), .in4(valid4), .in5(valid5), .in6(valid6),
    .in7(valid7), .out(valid), .sel(PC[6:4]));  // open: en

  assign Address = PC[19:4];

  // Other names for the same wires on the sheet: clk = Clock; cs = Chip_Select; drty = Dirty; en = Enable;
  //   Offset[1:0] = PC[3:2]; index[2:0] = PC[6:4]; tag[12:0] = PC[19:7]; RAM_Out_0[31:0] = Ram_0;
  //   RAM_Out_1[31:0] = Ram_1; RAM_Out_2[31:0] = Ram_2; RAM_Out_3[31:0] = Ram_3; rst = Reset; rt[3:0] = Read_Time

  // Notes on the sheet:
  //   Bank 0
  //   Bank 1
  //   Bank 2
  //   Bank 3
  //   Tag
  //   Tag Out
endmodule
